// Logisim project lab2.circ as structural Verilog: 1 circuit, main circuit main
module main (
  input  S1,
  input  S0,
  input  A1,
  input  A0,
  input  B1,
  input  B0,
  output X2,
  output Y7,
  output Y6,
  output X1,
  output Y5,
  output X0,
  output Y4,
  output Y3,
  output Y2,
  output Y1,
  output Y0
);

  wire and_1_out, and_2_out, n3_to_8_decoder_74138_1_p2, n3_to_8_decoder_74138_1_p4,
       n3_to_8_decoder_74138_1_p6, n3_to_8_decoder_74138_1_p7, n3_to_8_decoder_74138_1_p8,
       n3_to_8_decoder_74138_1_p9, n3_to_8_decoder_74138_1_p10, n3_to_8_decoder_74138_1_p11,
       n4_to_1_mux_x2_74153_1_p13, n4_to_1_mux_x2_74153_1_p14, not_1_out, or_1_out, or_2_out, or_3_out,
       or_4_out, xor_1_out, xor_2_out, xor_3_out, xor_4_out;

  not not_1 (not_1_out, A0);
  or or_1 (or_1_out, A1, B1);
  xor xor_1 (xor_1_out, B0, A0);
  or or_2 (or_2_out, B0, B1);
  and and_1 (and_1_out, B0, B1);
  or or_3 (or_3_out, B0, A0);
  xor xor_2 (xor_2_out, B1, A0);
  xor xor_3 (xor_3_out, B1, A1);
  or or_4 (or_4_out, B0, xor_2_out);
  and and_2 (and_2_out, not_1_out, B0);
  // _4_to_1_MUX__x2___74153 #(.Facing("east")) 4_to_1_mux_x2_74153_1: pin names not known; wires that end beside it: or_2_out, B1, and_1_out, not_1_out, or_3_out, or_4_out, and_1_out, or_3_out, 1'b0, A0, 1'b0, A1, n4_to_1_mux_x2_74153_1_p13, n4_to_1_mux_x2_74153_1_p14
  xor xor_4 (xor_4_out, and_2_out, xor_3_out);
  // _4_to_1_MUX__x2___74153 #(.Facing("east")) 4_to_1_mux_x2_74153_2: pin names not known; wires that end beside it: n4_to_1_mux_x2_74153_1_p13, 1'b0, B1, A1, xor_1_out, n4_to_1_mux_x2_74153_1_p14, 1'b0, 1'b1, 1'b0, 1'b0, X2, X0
  // _4_to_1_MUX__x2___74153 #(.Facing("east")) 4_to_1_mux_x2_74153_3: pin names not known; wires that end beside it: xor_4_out, or_1_out, B0, A0, S0, 1'b0, S0, S1, 1'b0, S1, X1
  // _3_to_8_decoder__74138 #(.Facing("south")) 3_to_8_decoder_74138_1: pin names not known; wires that end beside it: X0, n3_to_8_decoder_74138_1_p2, X1, n3_to_8_decoder_74138_1_p4, X2, n3_to_8_decoder_74138_1_p6, n3_to_8_decoder_74138_1_p7, n3_to_8_decoder_74138_1_p8, n3_to_8_decoder_74138_1_p9, n3_to_8_decoder_74138_1_p10, n3_to_8_decoder_74138_1_p11, 1'b1, 1'b0, 1'b0
  not not_2 (Y7, n3_to_8_decoder_74138_1_p11);
  not not_3 (Y6, n3_to_8_decoder_74138_1_p10);
  not not_4 (Y5, n3_to_8_decoder_74138_1_p9);
  not not_5 (Y4, n3_to_8_decoder_74138_1_p8);
  not not_6 (Y3, n3_to_8_decoder_74138_1_p7);
  not not_7 (Y2, n3_to_8_decoder_74138_1_p6);
  not not_8 (Y1, n3_to_8_decoder_74138_1_p4);
  not not_9 (Y0, n3_to_8_decoder_74138_1_p2);
endmodule
